# Fritzing sketch two_capacitor (saved by Fritzing 0.9.3b)
breadboards: 1

parts:
  Nano1 = Arduino Nano v2.3
  Fine-tune_Capacitor = Basic Servo
  Main_Capacitor = Basic Servo
  HC07 = Arduino BT

nets:
  N1: Nano1.D1TX, HC07.RX/D0
  N2: Nano1.D0RX, HC07.TX/D1
  GND: Nano1.GND, Fine-tune_Capacitor.gnd, Main_Capacitor.gnd, HC07.GND
  N3: Nano1.D8, Fine-tune_Capacitor.pulse
  N4: Nano1.D9, Main_Capacitor.pulse
  5V: Nano1.+5V, Fine-tune_Capacitor.vcc, Main_Capacitor.vcc, HC07.5V

notes:
  Magnetic Loop Bluetooth Remote Control (Alexloop or Homebrew Antenna)
  Two Capacitors
  2014
  By PU2CLR
